# Fritzing sketch diagram (saved by Fritzing 0.9.3b)

parts:
  U2 = ESP 32 DEVKIT DOIT
  RY1 = KF-301 Relay [package=THT]
  RY2 = KF-301 Relay [package=THT]
  RY3 = KF-301 Relay [package=THT]
  DHT2 = DHT11 Humitidy and Temperature Sensor (3 pins)
  LED1 = smd LED [color="Red (633nm)" package="1206 [SMD]"]
  LED2 = smd LED [color="Yellow (595nm)" package="1206 [SMD]"]

nets:
  N1: U2.Vin, RY1.power, RY2.power, RY3.power, DHT2.Plus
  GND: U2.GND, RY1.ground, RY2.ground, RY3.ground, DHT2.Gnd, LED2.cathode
  N2: U2.D13, U2.D14, RY1.signal, RY3.signal
  N3: U2.D12, RY2.signal
  N4: U2.D27, DHT2.Signal
  N5: U2.D26, LED1.anode
  N6: U2.D25, LED2.anode

custom parts:
  KF-301 Relay: KF-301 SPDT Relay module using SRD-05VDC-SL-C relay.
  DHT11 Humitidy and Temperature Sensor (3 pins): DHT11 Humidity and Temperature Sensor (3 pins).
